# Fritzing sketch PSD_schematic (saved by Fritzing 0.9.0b)
breadboards: 1

parts:
  Part1 = Arduino Uno (Rev3)
  R1 = Resistor [tolerance=±5% resistance=10k package=THT]
  C1 = Ceramic Capacitor [capacitance=100nF package="100 mil [THT, multilayer]"]
  Q1 = NPN-Transistor [package="TO92 [THT]"]
  R2 = Resistor [tolerance=±5% resistance=220 package=THT]
  LED1 = LED - 5mm [color="Red (633nm)" package="5 mm [THT]"]
  P1 = S1133 Si Photodiode [package="8mm Ceramic [THT]"]
  R3 = Resistor [tolerance=±5% resistance=220 package=THT]

nets:
  N1: Part1.A0, P1.cathode, R3.Pin_0
  N2: Part1.D9_PWM, R1.Pin_0
  N3: Part1.GND, C1.0, LED1.cathode, R3.Pin_1
  N4: Part1.5V, Q1.C, P1.anode
  N5: R1.Pin_1, C1.1, Q1.B
  N6: Q1.E, R2.Pin_1
  N7: R2.Pin_0, LED1.anode
